// Logisim project Prova 2.circ as structural Verilog
module Aaaa (
  input  A,
  input  B,
  input  C,
  input  D,
  output a_2,
  output b_2,
  output c_2
);

  wire and_1_out, and_2_out, and_3_out, and_4_out, and_5_out, and_6_out, and_7_out, and_8_out, not_1_out,
       not_2_out, not_3_out, not_4_out, not_5_out, not_6_out, not_7_out, not_8_out, not_9_out;

  not not_1 (not_1_out, A);
  not not_2 (not_2_out, B);
  and and_1 (and_1_out, not_1_out, not_2_out, not_3_out);
  not not_3 (not_3_out, D);
  not not_4 (not_4_out, B);
  and and_2 (and_2_out, not_4_out, C);
  and and_3 (and_3_out, C, not_5_out);
  not not_5 (not_5_out, D);
  and and_4 (and_4_out, A, D);
  and and_5 (and_5_out, C, not_6_out);
  not not_6 (not_6_out, D);
  not not_7 (not_7_out, C);
  and and_6 (and_6_out, B, not_7_out, D);
  not not_8 (not_8_out, C);
  and and_7 (and_7_out, not_8_out, D);
  and and_8 (and_8_out, B, not_9_out);
  not not_9 (not_9_out, D);
  or or_1 (a_2, and_1_out, and_2_out, and_3_out, and_4_out);
  or or_2 (b_2, and_5_out, and_6_out, A);
  or or_3 (c_2, and_7_out, and_8_out, A);
endmodule

module Comparador (
  input  A,
  input  B,
  input  Enable,
  output Maior,
  output Menor,
  output Igual
);

  wire and_3_out, and_4_out, not_1_out, not_2_out, not_3_out, not_4_out;

  not not_1 (not_1_out, B);
  not not_2 (not_2_out, A);
  not not_3 (not_3_out, A);
  not not_4 (not_4_out, B);
  and and_1 (Maior, A, not_1_out, Enable);
  and and_2 (Menor, not_2_out, B, Enable);
  and and_3 (and_3_out, not_3_out, not_4_out, Enable);
  and and_4 (and_4_out, A, B, Enable);
  or or_1 (Igual, and_3_out, and_4_out);
endmodule
